// Logisim project hw3.circ as structural Verilog
module _1_bit_Full_Adder (
  input  A,
  input  B,
  input  Carry_In,
  output Sum,
  output Carry_Out
);

  wire and_2_out, and_3_out, and_4_out, and_5_out, and_6_out, and_7_out, and_8_out;

  // AND_Gate and_1 has open pins: in0=A, in1=B, in2=Carry_In, out=open
  and and_2 (and_2_out, ~A, ~B, Carry_In);  // AND_Gate
  and and_3 (and_3_out, ~A, B, ~Carry_In);  // AND_Gate
  and and_4 (and_4_out, ~A, B, Carry_In);  // AND_Gate
  or or_1 (Sum, and_2_out, and_3_out, and_5_out, and_8_out);
  and and_5 (and_5_out, A, ~B, ~Carry_In);  // AND_Gate
  or or_2 (Carry_Out, and_4_out, and_6_out, and_7_out, and_8_out);
  and and_6 (and_6_out, A, ~B, Carry_In);  // AND_Gate
  and and_7 (and_7_out, A, B, ~Carry_In);  // AND_Gate
  and and_8 (and_8_out, A, B, Carry_In);

  // Notes on the sheet:
  //   Joon Ki Hong
endmodule

module _1_bit_ALU (
  input  A,
  input  B,
  input  Carry_In,
  input  in_4,
  input  in_5,
  input  in_6,
  output Addition_Only,
  output Output
);

  wire Add, AND, Increment, n1_bit_full_adder_3_sum, Negate, NOT, not_2_out, not_3_out, OR, Output_Add,
       Output_AND, Output_Increment, Output_Negate, Output_NOT, Output_OR, Output_Sub, Output_XOR, Subtract,
       XOR;

  _1_bit_Full_Adder u_1_bit_full_adder_1 (.A(A), .B(1'b1), .Carry_In(1'b0), .Sum(Output_Increment));  // open: Carry_Out
  not not_1 (Output_NOT, A);
  and and_1 (Add, ~in_6, in_5, in_4);  // AND_Gate
  and and_2 (Subtract, ~in_6, ~in_5, in_4);  // AND_Gate
  and and_3 (Increment, ~in_6, ~in_5, ~in_4);  // AND_Gate
  and and_4 (Negate, ~in_6, in_5, ~in_4);  // AND_Gate
  and and_5 (AND, in_6, ~in_5, in_4);  // AND_Gate
  and and_6 (OR, in_6, in_5, ~in_4);  // AND_Gate
  and and_7 (NOT, in_6, ~in_5, ~in_4);  // AND_Gate
  and and_8 (XOR, in_6, in_5, in_4);
  not not_2 (not_2_out, A);
  _1_bit_Full_Adder u_1_bit_full_adder_2 (
    .A(not_2_out), .B(1'b1), .Carry_In(1'b0), .Sum(Output_Negate));  // open: Carry_Out
  xor xor_1 (Output_XOR, A, B);
  _1_bit_Full_Adder u_1_bit_full_adder_3 (
    .A(not_3_out), .B(1'b1), .Carry_In(1'b0), .Sum(n1_bit_full_adder_3_sum));  // open: Carry_Out
  not not_3 (not_3_out, B);
  _1_bit_Full_Adder u_1_bit_full_adder_4 (
    .A(A), .B(n1_bit_full_adder_3_sum), .Carry_In(1'b0), .Sum(Output_Sub));  // open: Carry_Out
  and and_9 (Output_AND, A, B);
  or or_1 (Output_OR, A, B);
  _1_bit_Full_Adder u_1_bit_full_adder_5 (
    .A(A), .B(B), .Carry_In(Carry_In), .Sum(Output_Add), .Carry_Out(Addition_Only));
  Multiplexer #(.select(3), .disabled(0)) multiplexer_1 (
    .in0(Output_Add), .in1(Output_Sub), .in2(Output_Increment), .in3(Output_Negate), .in4(Output_AND),
    .in5(Output_OR), .in6(Output_NOT), .in7(Output_XOR), .out(Output), .sel({in_4, in_5, in_6}));  // open: en

  // Other names for the same wires on the sheet: S2 = in_6; S1 = in_5; S0 = in_4; Carry_Out = Addition_Only

  // Notes on the sheet:
  //   Increment
  //   NOT
  //   Joon Ki Hong
  //   XOR
  //   S0  S1  S2
  //   1   1   0
  //   1   0   0
  //   0   0   0
  //   0   1   0
  //   1   0   1
  //   0   1   1
  //   0   0   1
  //   1   1   1
  //   Negate
  //   Add
  //   Subtract
  //   Increment
  //   Negate
  //   AND
  //   OR
  //   NOT
  //   XOR
  //   AND
  //   Subtract
  //   OR
  //   Inputs
  //   Additon
endmodule

module _4_bit_Full_Adder (
  input  [3:0] A,
  input  [3:0] B,
  input  Carry_In,
  output Carry_Out,
  output [3:0] Sum
);

  wire n1_bit_full_adder_2_carry_out, n1_bit_full_adder_3_carry_out, n1_bit_full_adder_4_carry_out;

  _1_bit_Full_Adder u_1_bit_full_adder_1 (
    .A(A[3]), .B(B[3]), .Carry_In(n1_bit_full_adder_3_carry_out), .Sum(Sum[3]), .Carry_Out(Carry_Out));
  _1_bit_Full_Adder u_1_bit_full_adder_2 (
    .A(A[1]), .B(B[1]), .Carry_In(n1_bit_full_adder_4_carry_out), .Sum(Sum[1]),
    .Carry_Out(n1_bit_full_adder_2_carry_out));
  _1_bit_Full_Adder u_1_bit_full_adder_3 (
    .A(A[2]), .B(B[2]), .Carry_In(n1_bit_full_adder_2_carry_out), .Sum(Sum[2]),
    .Carry_Out(n1_bit_full_adder_3_carry_out));
  _1_bit_Full_Adder u_1_bit_full_adder_4 (
    .A(A[0]), .B(B[0]), .Carry_In(Carry_In), .Sum(Sum[0]), .Carry_Out(n1_bit_full_adder_4_carry_out));

  // Notes on the sheet:
  //   Joon Ki Hong
endmodule

module _4_bit_ALU (
  input  [3:0] A,
  input  [3:0] B,
  input  Carry_In,
  input  S0,
  input  S1,
  input  S2,
  output Carry_Out,
  output [3:0] Output
);

  wire Add, AND, Increment, Negate, NOT, OR, Subtract, XOR;
  wire [3:0] n4_bit_full_adder_2_sum, not_1_out, not_2_out, Output_Add, Output_AND, Output_Increment,
       Output_Negate, Output_NOT, Output_OR, Output_Subtract, Output_XOR;

  _4_bit_Full_Adder u_4_bit_full_adder_1 (
    .A(A), .B(n4_bit_full_adder_2_sum), .Carry_In(1'b0), .Sum(Output_Subtract));  // open: Carry_Out
  Decoder #(.select(3)) decoder_1 (
    .out0(Increment), .out1(NOT), .out2(Negate), .out3(OR), .out4(Subtract), .out5(AND), .out6(Add),
    .out7(XOR), .sel({S0, S1, S2}));  // open: en
  assign not_1_out = ~B;  // NOT_Gate not_1, 4 bits wide
  _4_bit_Full_Adder u_4_bit_full_adder_2 (
    .A(not_1_out), .B(4'b0001), .Carry_In(1'b0), .Sum(n4_bit_full_adder_2_sum));  // open: Carry_Out
  _4_bit_Full_Adder u_4_bit_full_adder_3 (
    .A(A), .B(4'b0001), .Carry_In(1'b0), .Sum(Output_Increment));  // open: Carry_Out
  _4_bit_Full_Adder u_4_bit_full_adder_4 (
    .A(not_2_out), .B(4'b0001), .Carry_In(1'b0), .Sum(Output_Negate));  // open: Carry_Out
  assign not_2_out = ~A;  // NOT_Gate not_2, 4 bits wide
  _4_bit_Full_Adder u_4_bit_full_adder_5 (.A(A), .B(B), .Carry_In(Carry_In), .Carry_Out(Carry_Out), .Sum(Output_Add));
  assign Output_AND = A & B;  // AND_Gate and_1, 4 bits wide
  assign Output_OR = A | B;  // OR_Gate or_1, 4 bits wide
  Multiplexer #(.select(3), .width(4), .disabled(0)) multiplexer_1 (
    .in0(Output_Increment), .in1(Output_NOT), .in2(Output_Negate), .in3(Output_OR), .in4(Output_Subtract),
    .in5(Output_AND), .in6(Output_Add), .in7(Output_XOR), .out(Output), .sel({S0, S1, S2}));  // open: en
  assign Output_NOT = ~A;  // NOT_Gate not_3, 4 bits wide
  assign Output_XOR = A ^ B;  // XOR_Gate xor_1, 4 bits wide

  // Notes on the sheet:
  //   Joon Ki Hong
  //   Subtraction
  //   Increment
  //   Negate
  //   AND
  //   Addition
  //   OR
  //   S0  S1  S2
  //   1   1   0
  //   1   0   0
  //   0   0   0
  //   0   1   0
  //   1   0   1
  //   0   1   1
  //   0   0   1
  //   1   1   1
  //   NOT
  //   Add
  //   Subtract
  //   Increment
  //   Negate
  //   AND
  //   OR
  //   NOT
  //   XOR
  //   XOR
endmodule
