// Logisim project hw4.circ as structural Verilog: 2 circuits, main circuit hw4
module hw4 (
  input  A
);

  wire clock_1_out, RESET_out, statemachine_1_c, statemachine_1_h;

  Button RESET (.out(RESET_out));
  Clock clock_1 (.out(clock_1_out));
  statemachine statemachine_1 (.A(A), .CLK(clock_1_out), .RES(RESET_out), .C(statemachine_1_c), .H(statemachine_1_h));
  LED C (.in(statemachine_1_c));
  LED H (.in(statemachine_1_h));

  // Notes on the sheet:
  //   Your name or you will lose points
  //   Joon Ki Hong
  //   Press the Reset button at any time to restart the state machine.
  //   C and H should be lit up when their corresponding outputs are 1.
endmodule

module statemachine (
  input  A,
  input  CLK,
  input  RES,
  output C,
  output H
);

  wire and_1_out, and_2_out, and_3_out, and_4_out, and_5_out, and_6_out, and_7_out, and_8_out, and_9_out,
       and_10_out, and_11_out, and_12_out, and_13_out, and_14_out, and_15_out, N0, N1, N2, S0, S1;

  and and_1 (and_1_out, S1, ~H);  // AND_Gate
  and and_2 (and_2_out, ~S1, H);  // AND_Gate
  and and_3 (and_3_out, S0, ~S1);  // AND_Gate
  and and_4 (and_4_out, ~S1, H);  // AND_Gate
  and and_5 (and_5_out, H, ~A);  // AND_Gate
  and and_6 (and_6_out, S1, ~H, A);  // AND_Gate
  Register #(.width(3)) register_1 (.D({N0, N1, N2}), .Q({S0, S1, H}), .clk(CLK), .clr(RES));  // open: en
  and and_7 (and_7_out, S0, ~S1);  // AND_Gate
  or or_1 (C, and_7_out, and_1_out, and_2_out);
  or or_2 (N1, and_3_out, and_4_out, and_5_out, and_6_out);
  and and_8 (and_8_out, ~S0, ~S1, ~H, A);  // AND_Gate
  and and_9 (and_9_out, S0, ~S1, ~A);  // AND_Gate
  and and_10 (and_10_out, H, ~A);  // AND_Gate
  and and_11 (and_11_out, ~S0, S1, H, A);  // AND_Gate
  and and_12 (and_12_out, ~S0, S1, ~H, ~A);  // AND_Gate
  and and_13 (and_13_out, S0, ~S1);  // AND_Gate
  and and_14 (and_14_out, S0, ~H, A);  // AND_Gate
  and and_15 (and_15_out, S0, H, ~A);  // AND_Gate
  or or_3 (N2, and_8_out, and_9_out, and_10_out);
  or or_4 (N0, and_13_out, and_14_out, and_15_out, and_11_out, and_12_out);

  // Other names for the same wires on the sheet: S2 = H

  // Notes on the sheet:
  //   N1 Output
  //   Inputs
  //   C Circuit
  //   H Circuit
  //   Nore: Do not move the input/output pins.  Do not add any additional inputs/outputs.
  //   CLK is the clock input and should be wired to the clock input of the register
  //   RES is the reset signal and should be wired to the '0' input of the register
  //   Build your minimized state machine in this subcircuit
  //   N0 Output
  //   N2 Output
  //   Outputs
endmodule
