// Logisim project LC3.circ as structural Verilog: 1 circuit, main circuit main
module main (
  input  [2:0] in_1,
  input  [2:0] in_2,
  input  [2:0] in_3,
  output [15:0] On_the_bus
);

  wire ADDR1MUX, CLK, GateALU, GateMARMUX, GateMDR, GatePC, LDCC, LDIR, LDMAR, LDMDR, LDPC, LDREG, MARMUX,
       MEMEN, MEMWE, RES, SRC2MUX;
  wire [1:0] ADDR2MUX, ALUK, PCMUX;
  wire [2:0] lc3logic_1_p4, NZP;
  wire [15:0] adder_1_out, adder_2_out, IR, lc3_reg_file_1_p4, lc3alu_1_p3, lc3alu_1_p4, MAR_p6, MDRtoMEM,
       MEMtoMAR, multiplexer_1_out, multiplexer_2_out, multiplexer_3_out, multiplexer_4_out,
       multiplexer_5_out, PC_q, sext_1_p2, sext_2_p2, sext_3_p2, sext_4_p2, zext_1_p2;

  Clock clock_1 (.out(CLK));
  Button button_1 (.out(RES));
  assign On_the_bus = GateMARMUX ? multiplexer_1_out : 16'bz;  // Controlled_Buffer controlled_buffer_1
  Multiplexer #(.width(16), .enable("false")) multiplexer_1 (
    .in0(zext_1_p2), .in1(adder_1_out), .out(multiplexer_1_out), .sel(MARMUX));
  // ZEXT zext_1: pin names not known; wires that end beside it: IR, zext_1_p2
  // SEXT sext_1: pin names not known; wires that end beside it: IR, sext_1_p2
  // SEXT sext_2: pin names not known; wires that end beside it: IR, sext_2_p2
  // SEXT sext_3: pin names not known; wires that end beside it: IR, sext_3_p2
  // DualOutRegister MAR: pin names not known; wires that end beside it: On_the_bus, LDMAR, CLK, RES, MEMtoMAR, MAR_p6
  Multiplexer #(.select(2), .width(16), .enable("false")) multiplexer_2 (
    .in0({16{1'b0}}), .in1(sext_3_p2), .in2(sext_2_p2), .in3(sext_1_p2), .out(multiplexer_2_out),
    .sel(ADDR2MUX));
  Register #(.width(16)) u_IR (.D(On_the_bus), .en(LDIR), .Q(IR), .clk(CLK), .clr(RES));
  Adder #(.width(16)) adder_1 (.a(multiplexer_2_out), .b(multiplexer_3_out), .out(adder_1_out));  // open: cin, cout
  Multiplexer #(.width(16), .enable("false")) multiplexer_3 (
    .in0(lc3alu_1_p4), .in1(PC_q), .out(multiplexer_3_out), .sel(ADDR1MUX));
  // SEXT sext_4: pin names not known; wires that end beside it: IR, sext_4_p2
  RAM #(.addrWidth(16), .dataWidth(16), .bus("separate")) ram_1 (
    .addr(MAR_p6), .din(MDRtoMEM), .data(MEMtoMAR), .str(MEMWE), .sel(MEMEN), .clk(CLK), .ld(1'b1), .clr(RES));
  Multiplexer #(.select(2), .width(16), .enable("false")) multiplexer_4 (
    .in0(adder_2_out), .in1(On_the_bus), .in2(adder_1_out), .in3(16'h3000), .out(multiplexer_4_out),
    .sel(PCMUX));
  Register #(.width(3)) u_NZP (.D(lc3logic_1_p4), .en(LDCC), .Q(NZP), .clk(CLK), .clr(RES));
  // LC3Logic lc3logic_1: pin names not known; wires that end beside it: lc3logic_1_p4[2], lc3logic_1_p4[1], On_the_bus, lc3logic_1_p4[0]
  // DualOutRegister MDR: pin names not known; wires that end beside it: MEMtoMAR, LDMDR, CLK, RES, On_the_bus, MDRtoMEM
  Register #(.width(16)) PC (.D(multiplexer_4_out), .en(LDPC), .Q(PC_q), .clk(CLK), .clr(RES));
  assign On_the_bus = GateMDR ? MDRtoMEM : 16'bz;  // Controlled_Buffer controlled_buffer_2
  assign On_the_bus = GatePC ? PC_q : 16'bz;  // Controlled_Buffer controlled_buffer_3
  Adder #(.width(16)) adder_2 (.a(PC_q), .b(16'h1), .out(adder_2_out));  // open: cin, cout
  Multiplexer #(.width(16), .enable("false")) multiplexer_5 (
    .in0(sext_4_p2), .in1(lc3_reg_file_1_p4), .out(multiplexer_5_out), .sel(SRC2MUX));
  // LC3ALU lc3alu_1: pin names not known; wires that end beside it: ALUK, multiplexer_5_out, lc3alu_1_p3, lc3alu_1_p4
  assign On_the_bus = GateALU ? lc3alu_1_p3 : 16'bz;  // Controlled_Buffer controlled_buffer_4
  // LC3StateMachine lc3statemachine_1: pin names not known; wires that end beside it: IR, NZP, CLK, RES, LDMAR, LDMDR, LDIR, LDREG, LDCC, LDPC, GatePC, GateMDR, GateALU, GateMARMUX, PCMUX, SRC2MUX, ADDR1MUX, ADDR2MUX, MARMUX, ALUK, MEMWE, MEMEN
  // LC3_Reg_File lc3_reg_file_1: pin names not known; wires that end beside it: in_3, LDREG, in_2, lc3_reg_file_1_p4, On_the_bus, lc3alu_1_p4, CLK, RES, in_1

  // Other names for the same wires on the sheet: DR[2:0] = in_3; SRC1[2:0] = in_1; SRC2[2:0] = in_2

  // Notes on the sheet:
  //   Value Currently
  //   Use these to select which register you are using for your operations
  //   POKE ME!
endmodule
