// Logisim project lab3part1.circ as structural Verilog: 1 circuit, main circuit main circuit
module main_circuit (
  input  in_1,
  input  in_2,
  input  in_3,
  input  in_4,
  output out_5
);

  wire transistor_3_out, transistor_5_out, transistor_6_out, transistor_9_out;

  Transistor transistor_1 (.in(1'b1), .out(out_5), .gate(in_1));
  Transistor #(.\type ("n")) transistor_2 (.in(transistor_3_out), .out(out_5), .gate(in_1));
  Transistor #(.\type ("n")) transistor_3 (.in(1'b0), .out(transistor_3_out), .gate(in_4));
  Transistor transistor_4 (.in(1'b1), .out(out_5), .gate(in_4));
  Transistor transistor_5 (.in(1'b1), .out(transistor_5_out), .gate(in_2));
  Transistor transistor_6 (.in(transistor_5_out), .out(transistor_6_out), .gate(in_3));
  Transistor #(.\type ("n")) transistor_7 (.in(1'b0), .out(transistor_6_out), .gate(in_3));
  Transistor #(.\type ("n")) transistor_8 (.in(1'b0), .out(transistor_6_out), .gate(in_2));
  Transistor transistor_9 (.in(1'b1), .out(transistor_9_out), .gate(transistor_6_out));
  Transistor #(.\type ("n")) transistor_10 (.in(1'b0), .out(transistor_9_out), .gate(transistor_6_out));

  // Notes on the sheet:
  //   Joon Ki Hong
endmodule
