// Logisim project lab4Part2.circ as structural Verilog: 1 circuit, main circuit main circuit
module main_circuit (
  input  in_1,
  input  in_2,
  input  in_3,
  input  in_4,
  input  in_5,
  input  in_6,
  input  A,
  input  B,
  input  C,
  input  D,
  input  E,
  input  F,
  input  G,
  input  H,
  input  S1,
  input  S2,
  input  S3,
  output out_18,
  output out_19,
  output out_20,
  output out_21,
  output out_22,
  output out_23,
  output out_24
);

  wire and_1_out, and_6_out, and_7_out, and_8_out, and_9_out, and_10_out, and_11_out, and_12_out, and_13_out,
       not_1_out, or_3_out;

  and and_1 (and_1_out, A, ~S1, ~S2, ~S3);  // AND_Gate
  and and_2 (out_18, in_4, in_5);
  and and_3 (out_20, ~in_4, in_5);  // AND_Gate
  and and_4 (out_21, in_4, ~in_5);  // AND_Gate
  and and_5 (out_23, ~in_4, ~in_5);  // AND_Gate
  and and_6 (and_6_out, B, ~S1, ~S2, S3);  // AND_Gate
  and and_7 (and_7_out, C, ~S1, S2, S3);  // AND_Gate
  and and_8 (and_8_out, D, S1, S2, S3);
  and and_9 (and_9_out, E, S1, S2, ~S3);  // AND_Gate
  or or_1 (out_24, and_1_out, and_6_out, and_7_out, and_8_out, and_9_out, and_10_out, and_11_out, and_13_out);
  not not_1 (not_1_out, in_2);
  or or_2 (out_22, in_1, in_2);
  and and_10 (and_10_out, F, S1, ~S2, ~S3);  // AND_Gate
  and and_11 (and_11_out, G, S1, ~S2, S3);  // AND_Gate
  and and_12 (and_12_out, not_1_out, in_3);
  or or_3 (or_3_out, out_22, in_3, in_6);
  and and_13 (and_13_out, H, ~S1, S2, ~S3);  // AND_Gate
  or or_4 (out_19, in_1, and_12_out);

  // Notes on the sheet:
  //   2 Input Decoder
  //   Joon Ki Hong
  //   8 input/3 Select Line MUX
  //   4 Input Encoder
endmodule
