// Logisim project lab6part2.circ as structural Verilog: 2 circuits, main circuit main circuit
module main_circuit (
  input  Di_3,
  input  Di_2,
  input  Di_1,
  input  Di_0,
  input  WE,
  input  [2:0] in_6,
  output D_3,
  output D_2,
  output D_1,
  output D_0
);

  _2_by_8_bit_memory u_2_by_8_bit_memory_1 (.WE(WE), .Di_1(Di_3), .Di_0(Di_2), .Select(in_6), .D_1(D_3), .D_0(D_2));
  _2_by_8_bit_memory u_2_by_8_bit_memory_2 (.WE(WE), .Di_1(Di_1), .Di_0(Di_0), .Select(in_6), .D_1(D_1), .D_0(D_0));

  // Other names for the same wires on the sheet: Select[2:0] = in_6

  // Notes on the sheet:
  //   Joon Ki Hong
  //   4 by 8 bit memory
endmodule

module _2_by_8_bit_memory (
  input  Di_1,
  input  Di_0,
  input  WE,
  input  [2:0] Select,
  output D_1,
  output D_0
);

  wire and_1_out, and_2_out, and_3_out, and_4_out, and_5_out, and_6_out, and_7_out, and_8_out, clock_1_out,
       clock_2_out, clock_3_out, clock_4_out, clock_5_out, clock_6_out, clock_7_out, clock_8_out,
       clock_9_out, clock_10_out, clock_11_out, clock_12_out, clock_13_out, clock_14_out, clock_15_out,
       clock_16_out, decoder_1_out0, decoder_1_out1, decoder_1_out2, decoder_1_out3, decoder_1_out4,
       decoder_1_out5, decoder_1_out6, decoder_1_out7, register_1_q, register_2_q, register_3_q,
       register_4_q, register_5_q, register_6_q, register_7_q, register_8_q, register_9_q, register_10_q,
       register_11_q, register_12_q, register_13_q, register_14_q, register_15_q, register_16_q;

  Decoder #(.select(3)) decoder_1 (
    .out0(decoder_1_out0), .out1(decoder_1_out1), .out2(decoder_1_out2), .out3(decoder_1_out3),
    .out4(decoder_1_out4), .out5(decoder_1_out5), .out6(decoder_1_out6), .out7(decoder_1_out7), .sel(Select));  // open: en
  and and_1 (and_1_out, decoder_1_out0, WE);
  and and_2 (and_2_out, decoder_1_out1, WE);
  and and_3 (and_3_out, decoder_1_out2, WE);
  and and_4 (and_4_out, decoder_1_out3, WE);
  and and_5 (and_5_out, decoder_1_out4, WE);
  and and_6 (and_6_out, decoder_1_out5, WE);
  and and_7 (and_7_out, decoder_1_out6, WE);
  and and_8 (and_8_out, decoder_1_out7, WE);
  Register #(.width(1)) register_1 (.D(Di_1), .en(and_1_out), .Q(register_1_q), .clk(clock_1_out));  // open: clr
  Clock clock_1 (.out(clock_1_out));
  Register #(.width(1)) register_2 (.D(Di_1), .en(and_2_out), .Q(register_2_q), .clk(clock_2_out));  // open: clr
  Clock clock_2 (.out(clock_2_out));
  Register #(.width(1)) register_3 (.D(Di_1), .en(and_3_out), .Q(register_3_q), .clk(clock_3_out));  // open: clr
  Clock clock_3 (.out(clock_3_out));
  Register #(.width(1)) register_4 (.D(Di_1), .en(and_4_out), .Q(register_4_q), .clk(clock_4_out));  // open: clr
  Clock clock_4 (.out(clock_4_out));
  Register #(.width(1)) register_5 (.D(Di_1), .en(and_5_out), .Q(register_5_q), .clk(clock_5_out));  // open: clr
  Clock clock_5 (.out(clock_5_out));
  Register #(.width(1)) register_6 (.D(Di_1), .en(and_6_out), .Q(register_6_q), .clk(clock_6_out));  // open: clr
  Clock clock_6 (.out(clock_6_out));
  Register #(.width(1)) register_7 (.D(Di_1), .en(and_7_out), .Q(register_7_q), .clk(clock_7_out));  // open: clr
  Clock clock_7 (.out(clock_7_out));
  Register #(.width(1)) register_8 (.D(Di_1), .en(and_8_out), .Q(register_8_q), .clk(clock_8_out));  // open: clr
  Clock clock_8 (.out(clock_8_out));
  Register #(.width(1)) register_9 (.D(Di_0), .en(and_1_out), .Q(register_9_q), .clk(clock_9_out));  // open: clr
  Clock clock_9 (.out(clock_9_out));
  Register #(.width(1)) register_10 (.D(Di_0), .en(and_2_out), .Q(register_10_q), .clk(clock_10_out));  // open: clr
  Clock clock_10 (.out(clock_10_out));
  Register #(.width(1)) register_11 (.D(Di_0), .en(and_3_out), .Q(register_11_q), .clk(clock_11_out));  // open: clr
  Clock clock_11 (.out(clock_11_out));
  Register #(.width(1)) register_12 (.D(Di_0), .en(and_4_out), .Q(register_12_q), .clk(clock_12_out));  // open: clr
  Clock clock_12 (.out(clock_12_out));
  Register #(.width(1)) register_13 (.D(Di_0), .en(and_5_out), .Q(register_13_q), .clk(clock_13_out));  // open: clr
  Clock clock_13 (.out(clock_13_out));
  Register #(.width(1)) register_14 (.D(Di_0), .en(and_6_out), .Q(register_14_q), .clk(clock_14_out));  // open: clr
  Clock clock_14 (.out(clock_14_out));
  Register #(.width(1)) register_15 (.D(Di_0), .en(and_7_out), .Q(register_15_q), .clk(clock_15_out));  // open: clr
  Clock clock_15 (.out(clock_15_out));
  Register #(.width(1)) register_16 (.D(Di_0), .en(and_8_out), .Q(register_16_q), .clk(clock_16_out));  // open: clr
  Clock clock_16 (.out(clock_16_out));
  Multiplexer #(.select(3), .disabled(0)) multiplexer_1 (
    .in0(register_1_q), .in1(register_2_q), .in2(register_3_q), .in3(register_4_q), .in4(register_5_q),
    .in5(register_6_q), .in6(register_7_q), .in7(register_8_q), .out(D_1), .sel(Select));  // open: en
  Multiplexer #(.select(3), .disabled(0)) multiplexer_2 (
    .in0(register_9_q), .in1(register_10_q), .in2(register_11_q), .in3(register_12_q), .in4(register_13_q),
    .in5(register_14_q), .in6(register_15_q), .in7(register_16_q), .out(D_0), .sel(Select));  // open: en
endmodule
