// Logisim project lab7part1.circ as structural Verilog: 1 circuit, main circuit main circuit
module main_circuit (
  input  in_1
);

  wire and_2_out, and_3_out, clock_1_out, Input_0, Input_1, Input_2, S_0, S_1, S_2;

  and and_1 (Input_0, S_1, S_2);
  and and_2 (and_2_out, ~S_0, ~S_1, S_2);  // AND_Gate
  and and_3 (and_3_out, S_1, ~S_2);  // AND_Gate
  and and_4 (Input_2, ~S_0, ~S_2);  // AND_Gate
  Register #(.width(3)) register_1 (
    .D({Input_2, Input_1, Input_0}), .en(in_1), .Q({S_2, S_1, S_0}), .clk(clock_1_out));  // open: clr
  Clock clock_1 (.out(clock_1_out));
  or or_1 (Input_1, and_2_out, and_3_out);
endmodule
