// Logisim project tl1.circ as structural Verilog: 1 circuit, main circuit main circuit
module main_circuit (
  input  in_1,
  input  in_2,
  input  in_3,
  input  in_4,
  input  in_5,
  input  in_6,
  input  in_7,
  input  [2:0] in_8,
  input  [2:0] in_9,
  input  [2:0] in_10,
  input  [2:0] in_11,
  input  in_12,
  input  in_13,
  output out_14,
  output out_15,
  output [2:0] out_16
);

  wire and_1_out, and_2_out, and_3_out, and_4_out, and_5_out, and_6_out, and_7_out, and_8_out, and_9_out,
       and_10_out, and_11_out, and_12_out, and_13_out, and_14_out, and_15_out, and_16_out, and_17_out,
       and_18_out, and_19_out, and_20_out, and_21_out, and_22_out, transistor_1_out, transistor_2_out,
       transistor_3_out;

  and and_1 (and_1_out, in_8[2], and_3_out);
  and and_2 (and_2_out, in_8[1], and_3_out);
  or or_1 (out_16[2], and_1_out, and_6_out, and_9_out, and_21_out);
  and and_3 (and_3_out, in_12, in_13);
  and and_4 (and_4_out, in_8[0], and_3_out);
  and and_5 (and_5_out, in_9[1], and_7_out);
  and and_6 (and_6_out, in_9[2], and_7_out);
  or or_2 (out_16[1], and_2_out, and_5_out, and_18_out, and_22_out);
  and and_7 (and_7_out, ~in_12, in_13);  // AND_Gate
  and and_8 (and_8_out, in_9[0], and_7_out);
  and and_9 (and_9_out, in_10[2], and_16_out);
  and and_10 (and_10_out, ~in_1, ~in_2, ~in_4);  // AND_Gate
  and and_11 (and_11_out, ~in_1, ~in_2, in_4);  // AND_Gate
  and and_12 (and_12_out, ~in_1, in_2, ~in_4);  // AND_Gate
  and and_13 (and_13_out, in_1, ~in_2, ~in_4);  // AND_Gate
  and and_14 (and_14_out, in_1, in_2, ~in_4);  // AND_Gate
  and and_15 (and_15_out, in_1, in_2, in_4);
  and and_16 (and_16_out, ~in_12, ~in_13);  // AND_Gate
  and and_17 (and_17_out, in_10[0], and_16_out);
  and and_18 (and_18_out, in_10[1], and_16_out);
  or or_3 (out_16[0], and_4_out, and_8_out, and_17_out, and_20_out);
  and and_19 (and_19_out, in_12, ~in_13);  // AND_Gate
  and and_20 (and_20_out, in_11[0], and_19_out);
  and and_21 (and_21_out, in_11[2], and_19_out);
  and and_22 (and_22_out, in_11[1], and_19_out);
  or or_4 (out_14, and_10_out, and_11_out, and_12_out, and_13_out, and_14_out, and_15_out);
  Transistor transistor_1 (.in(1'b1), .out(transistor_1_out), .gate(in_3));
  Transistor transistor_2 (.in(transistor_1_out), .out(transistor_2_out), .gate(in_5));
  Transistor transistor_3 (.in(transistor_2_out), .out(transistor_3_out), .gate(in_6));
  Transistor transistor_4 (.in(transistor_3_out), .out(out_15), .gate(in_7));
  Transistor #(.\type ("n")) transistor_5 (.in(1'b0), .out(out_15), .gate(in_3));
  Transistor #(.\type ("n")) transistor_6 (.in(1'b0), .out(out_15), .gate(in_5));
  Transistor #(.\type ("n")) transistor_7 (.in(1'b0), .out(out_15), .gate(in_7));
  Transistor #(.\type ("n")) transistor_8 (.in(1'b0), .out(out_15), .gate(in_6));

  // Notes on the sheet:
  //   Joon Ki Hong
  //   Part 2 -Multiplexor
  //   Part 1 - Truth Table
  //   Part 3- Transistor
endmodule
