// Logisim project timedlab2.circ as structural Verilog: 2 circuits, main circuit main circuit
module main_circuit (
  input  in_1,
  input  TEST
);

  wire clock_1_out, multiplexer_1_out, RAND, statemachine_1_b, statemachine_1_g, statemachine_1_led,
       statemachine_1_r;

  Multiplexer #(.disabled(0), .enable("false")) multiplexer_1 (
    .in0(RAND), .in1(in_1), .out(multiplexer_1_out), .sel(TEST));
  Clock clock_1 (.out(clock_1_out));
  LED led_1 (.in(statemachine_1_led));
  statemachine statemachine_1 (
    .CLK(clock_1_out), .RAND(multiplexer_1_out), .LED(statemachine_1_led), .R(statemachine_1_r),
    .G(statemachine_1_g), .B(statemachine_1_b));
  // TL tl_1: pin names not known; wires that end beside it: statemachine_1_r, statemachine_1_g, statemachine_1_b, RAND

  // Notes on the sheet:
  //   Joon Ki Hong
  //   Use both of the above input pins to test your circuit.
  //   To test make sure the input pin labeled TEST is 1
  //   You may then vary the RAND input by using the second input
  //   Do not modify anything in this file
endmodule

module statemachine (
  input  CLK,
  input  RAND,
  output LED,
  output R,
  output G,
  output B
);

  wire and_1_out, and_2_out, and_3_out, and_4_out, and_5_out, and_6_out, and_7_out, and_8_out, and_9_out,
       and_10_out, and_11_out, and_12_out, and_13_out, and_14_out, and_15_out, and_16_out, and_17_out, N0,
       N1, N2, S0, S1, S2;

  and and_1 (and_1_out, ~S0, S1, S2);  // AND_Gate
  or or_1 (R, and_1_out, and_2_out);
  and and_2 (and_2_out, S0, S1, ~S2);  // AND_Gate
  and and_3 (and_3_out, ~S0, S1, S2);  // AND_Gate
  or or_2 (N0, and_3_out, and_4_out, and_5_out);
  and and_4 (and_4_out, S0, S1, S2);
  and and_5 (and_5_out, S0, S1, ~S2);  // AND_Gate
  Register #(.width(3)) register_1 (.D({N2, N1, N0}), .en(1'b1), .Q({S2, S1, S0}), .clk(CLK));  // open: clr
  and and_6 (and_6_out, S0, S1, S2);
  and and_7 (and_7_out, S0, S1, ~S2);  // AND_Gate
  and and_8 (and_8_out, S0, ~S1, ~S2);  // AND_Gate
  or or_3 (G, and_6_out, and_7_out, and_8_out);
  and and_9 (and_9_out, ~S0, ~S1, S2);  // AND_Gate
  and and_10 (and_10_out, ~S0, S1, S2);  // AND_Gate
  or or_4 (N1, and_9_out, and_10_out, and_11_out, and_12_out);
  and and_11 (and_11_out, S0, S1, S2, RAND);
  and and_12 (and_12_out, S0, S1, ~S2, ~RAND);  // AND_Gate
  and and_13 (and_13_out, ~S0, ~S1, S2);  // AND_Gate
  and and_14 (and_14_out, S0, ~S1, ~S2);  // AND_Gate
  or or_5 (B, and_13_out, and_14_out);
  and and_15 (and_15_out, ~S0, ~S1, ~S2, RAND);  // AND_Gate
  and and_16 (and_16_out, ~S0, ~S1, S2);  // AND_Gate
  and and_17 (and_17_out, ~S0, S1, S2, ~RAND);  // AND_Gate
  and and_18 (LED, ~S0, ~S1, ~S2);  // AND_Gate
  or or_6 (N2, and_15_out, and_16_out, and_17_out);

  // Notes on the sheet:
  //   Joon Ki Hong
  //   Red Circuit
  //   N0 Circuit
  //   Green Circuit
  //   N1 Circuit
  //   Do not add/move/remove any inputs/outputs.
  //   Implement your state machine here.
  //   Blue Circuit
  //   N2 Circuit
  //   LED Circuit
endmodule
