// Logisim project p5_circuit.circ as structural Verilog: 1 circuit, main circuit main
module main (
  input  [31:0] FBUF,
  input  [31:0] R1b,
  output RpR1
);

  wire Add, Addi, and_1_out, and_2_out, and_3_out, BEQ, Jalr, LW, NAND, or_1_out, or_2_out, or_3_out,
       or_4_out, or_5_out, Rx_R1, Ry_R1, Rz_R1, SW;

  Decoder #(.select(4)) decoder_1 (
    .out0(Add), .out1(Addi), .out2(SW), .out3(BEQ), .out4(NAND), .out5(LW), .out6(Jalr), .sel(FBUF[31:28]),
    .en(1'b1));  // open: out7, out8, out9, out10, out11, out12, out13, out14, out15
  Decoder #(.select(4)) decoder_2 (
    .out1(Rz_R1), .sel(FBUF[3:0]), .en(1'b1));  // open: out0, out2, out3, out4, out5, out6, out7, out8, out9, out10, out11, out12, out13, out14, out15
  or or_1 (or_1_out, Ry_R1, Rz_R1);
  or or_2 (or_2_out, Add, NAND);
  and and_1 (and_1_out, or_1_out, R1b[31], or_2_out);
  or or_3 (or_3_out, Ry_R1, Rx_R1);
  or or_4 (or_4_out, SW, BEQ);
  or or_5 (or_5_out, Jalr, LW, Addi);
  and and_2 (and_2_out, or_3_out, R1b[31], or_4_out);
  and and_3 (and_3_out, Rx_R1, R1b[31], or_5_out);
  Decoder #(.select(4)) decoder_3 (
    .out1(Rx_R1), .sel(FBUF[27:24]), .en(1'b1));  // open: out0, out2, out3, out4, out5, out6, out7, out8, out9, out10, out11, out12, out13, out14, out15
  Decoder #(.select(4)) decoder_4 (
    .out1(Ry_R1), .sel(FBUF[23:20]), .en(1'b1));  // open: out0, out2, out3, out4, out5, out6, out7, out8, out9, out10, out11, out12, out13, out14, out15
  or or_6 (RpR1, and_2_out, and_1_out, and_3_out);

  // Other names for the same wires on the sheet: OpCode[3:0] = FBUF[31:28]; R1b_1 = R1b[31]

  // Notes on the sheet:
  //   Rp for R1
endmodule
